# Fritzing sketch Event2ObjectRemoval (saved by Fritzing 0.9.3b)

parts:
  Arduino = Arduino Uno (Rev3)
  J1 = Basic Servo
  VCC1 = Battery
  S1 = Pushbutton [package=THT]
  J2 = Basic Servo

nets:
  N1: Arduino.D9_PWM, J1.pulse
  N2: Arduino.D10_PWM/SS, J2.pulse
  5V: Arduino.5V, J2.vcc
  GND: Arduino.GND, J1.gnd, J2.gnd
  VIN: Arduino.VIN, J1.vcc
  N3: VCC1.-, S1.leg1
